# Fritzing sketch BT_Robot (saved by Fritzing 0.9.3b)

parts:
  Part1 = Arduino Nano (Rev3.0)
  hc-sr1 = hc-sr04
  S1 = H-Bridge with L298N
  M1 = DC Motor
  M2 = DC Motor
  Keyes1 = Keyes IR Infrared Sensor Switch Module
  J1 = Basic Servo
  Keyes2 = Keyes IR Infrared Sensor Switch Module
  Keyes3 = Keyes IR Infrared Sensor Switch Module
  VCC1 = Battery block 9V
  Part2 = Bluetooth HC-05 Macho

nets:
  GND: Part1.GND, hc-sr1.GND, S1.GND, Keyes1.GND, J1.gnd, Keyes2.GND, Keyes3.GND, VCC1.-
  N1: Part1.D3, S1.IN3
  N2: Part1.D4, S1.IN1
  N3: Part1.D5, S1.IN2
  N4: Part1.D6, S1.ENA, S1.ENB
  N5: Part1.D7, S1.IN4
  N6: Part1.D8, Keyes3.out
  N7: Part1.D9, J1.pulse
  N8: Part1.D10, Keyes2.out
  N9: Part1.D11/MOSI, Part2.RXD
  N10: Part1.D12/MISO, Part2.TXD
  VIN: Part1.VIN, S1.5V
  VCC: Part1.5V, Keyes1.VCC, Keyes2.VCC, Keyes3.VCC
  N11: Part1.A1, hc-sr1.Echo
  N12: Part1.A0, hc-sr1.Trig
  N13: Part1.D13/SCK, Keyes1.out
  VCC_2: hc-sr1.VCC, J1.vcc
  N14: S1.12V, VCC1.+
  N15: S1.M1-01, M1.pin_2
  N16: S1.M1-02, M1.pin_1
  N17: S1.M2-01, M2.pin_2
  N18: S1.M2-02, M2.pin_1

custom parts:
  H-Bridge with L298N: h-bridge
  Keyes IR Infrared Sensor Switch Module: An infrared obstacle detector
