# Fritzing sketch Node_MCU_Robot (saved by Fritzing 0.9.3b)

parts:
  hc-sr2 = hc-sr04
  S2 = H-Bridge with L298N
  M3 = DC Motor
  M4 = DC Motor
  Keyes4 = Keyes IR Infrared Sensor Switch Module
  Keyes5 = Keyes IR Infrared Sensor Switch Module
  Keyes6 = Keyes IR Infrared Sensor Switch Module
  J2 = Basic Servo
  VCC2 = Battery block 9V
  U1 = NodeMCU V1.0

nets:
  VCC: hc-sr2.VCC, J2.vcc
  N1: hc-sr2.Trig, U1.D7
  N2: hc-sr2.Echo, U1.D6
  GND: hc-sr2.GND, S2.GND, Keyes4.GND, Keyes5.GND, Keyes6.GND, J2.gnd, VCC2.-, U1.GND
  N3: S2.12V, VCC2.+
  5V: S2.5V, U1.Vin
  N4: S2.ENA, S2.ENB, U1.RX
  N5: S2.IN1, U1.D1
  N6: S2.IN2, U1.D2
  N7: S2.IN3, U1.D3
  N8: S2.IN4, U1.D4
  N9: S2.M1-01, M4.pin_2
  N10: S2.M1-02, M4.pin_1
  N11: S2.M2-01, M3.pin_2
  N12: S2.M2-02, M3.pin_1
  VCC_2: Keyes4.VCC, Keyes5.VCC, Keyes6.VCC
  N13: Keyes4.out, U1.SD2
  N14: Keyes5.out, U1.SD3
  N15: Keyes6.out, U1.TX
  N16: J2.pulse, U1.D8

custom parts:
  H-Bridge with L298N: h-bridge
  Keyes IR Infrared Sensor Switch Module: An infrared obstacle detector
  NodeMCU V1.0: ESP8266 based NodeMCU
